# Fritzing sketch IntroductionToArduino-BareBreadboardSetup-WithLevelShifter-V1 (saved by Fritzing 0.9.6b)
breadboards: 1

parts:
  Heltec_New_WiFi_Kit_1 = Heltec New WiFi Kit 32 [part_number=ZC-47]
  Part1 = I2C level shifter bidirectional  # not connected
  U1 = 74HC595 [package="DIP16 [THT]"]  # not connected
  U2 = Optocoupler [package=THT]  # not connected
  U3 = Vibration Motor- ROB-08449 [package=vibe-motor-10mm]  # not connected
  S1 = Momentary Switch [package=ksa_sealed_tac_switch]  # not connected

nets:
  N1: Heltec_New_WiFi_Kit_1.pin_16, Heltec_New_WiFi_Kit_1.pin_20
  N2: Heltec_New_WiFi_Kit_1.pin_18, Heltec_New_WiFi_Kit_1.pin_19
  N3: Heltec_New_WiFi_Kit_1.pin_21, Heltec_New_WiFi_Kit_1.pin_15
