# Fritzing sketch arduino-Lesson10-WeimosD1WiringDiagram-V1 (saved by Fritzing 0.9.6b)
breadboards: 1

parts:
  NEOPIXEL1 = Neopixel Strip -- Black (30/m) [part_number=1376]
  JACK1 = 2.1mm Barrel Jack with Terminal Block
  C1 = Electrolytic Capacitor [capacitance=1000µF voltage=35V package="300 mil [THT, electrolytic]"]
  D1 = Diode [package=diode-hv]
  Part4 = I2C level shifter bidirectional
  WeMos_D1_Mini1 = WeMos D1 Mini

nets:
  GND: NEOPIXEL1.GND, JACK1.NEG, C1.-, Part4.GND, WeMos_D1_Mini1.G
  N1: NEOPIXEL1.Din, Part4.HV1
  N2: NEOPIXEL1.+5V, JACK1.POS, C1.+, D1.A
  N3: D1.C, Part4.HV, WeMos_D1_Mini1.5V
  N4: Part4.LV, WeMos_D1_Mini1.3V3
  N5: Part4.LV1, WeMos_D1_Mini1.D4

notes:
  SEE NOTE!!!
  Pick one rail for *protected* 5V [red recommended]
  Keep LED Data and Power connections at opposite end of board
  1000uF
  Diode prevents USB from powering LEDs
  "Band towards board"
  DO NOT FORGET THE 3V3 JUMPER!
  Pick one rail for *unprotected* 5V, one for ground

custom parts:
  Neopixel Strip -- Black (30/m): These NeoPixel strips have 30 digitally-addressable pixel LEDs per meter and are very affordable and are only 12.5 mm wide, 10 mm if you remove the strip from the casing.
  WeMos D1 Mini: The D1 mini is a mini wifi board based on ESP-8266EX.
