# Fritzing sketch arduino-Lesson10-WiringDiagram-V3 (saved by Fritzing 0.9.6b)
breadboards: 1

parts:
  Heltec_New_WiFi_Kit_1 = Heltec New WiFi Kit 32 [part_number=ZC-47]
  NEOPIXEL1 = Neopixel Strip -- Black (30/m) [part_number=1376]
  JACK1 = 2.1mm Barrel Jack with Terminal Block
  C1 = Electrolytic Capacitor [capacitance=1000µF voltage=35V package="300 mil [THT, electrolytic]"]
  D1 = Diode [package=diode-hv]
  Part4 = I2C level shifter bidirectional

nets:
  N1: Heltec_New_WiFi_Kit_1.pin_27, Part4.LV1
  N2: Heltec_New_WiFi_Kit_1.pin_16, Heltec_New_WiFi_Kit_1.pin_20, D1.C, Part4.LV, Part4.HV
  GND: Heltec_New_WiFi_Kit_1.pin_18, Heltec_New_WiFi_Kit_1.pin_19, NEOPIXEL1.GND, JACK1.NEG, C1.-, Part4.GND
  N3: Heltec_New_WiFi_Kit_1.pin_21, Heltec_New_WiFi_Kit_1.pin_15
  N4: NEOPIXEL1.Din, Part4.HV1
  N5: NEOPIXEL1.+5V, JACK1.POS, C1.+, D1.A

notes:
  SEE NOTE!!!
  Pick one rail for *protected* 5V [red recommended]
  Keep LED Data and Power connections at opposite end of board
  1000uF
  Diode prevents USB from powering LEDs
  "Band towards board"
  DO NOT FORGET THE 3V3 JUMPER!
  Pick one rail for *unprotected* 5V, one for ground

custom parts:
  Neopixel Strip -- Black (30/m): These NeoPixel strips have 30 digitally-addressable pixel LEDs per meter and are very affordable and are only 12.5 mm wide, 10 mm if you remove the strip from the casing.
