# Fritzing sketch arduino-Lesson11-WiringDiagram-V1 (saved by Fritzing 0.9.6b)
breadboards: 1

parts:
  Heltec_New_WiFi_Kit_1 = Heltec New WiFi Kit 32 [part_number=ZC-47]
  NEOPIXEL1 = Neopixel Strip -- Black (30/m) [part_number=1376]
  JACK1 = 2.1mm Barrel Jack with Terminal Block
  C1 = Electrolytic Capacitor [capacitance=1000µF voltage=35V package="300 mil [THT, electrolytic]"]
  D1 = Diode [package=diode-hv]
  Part4 = I2C level shifter bidirectional  # not connected
  R1 = Resistor [tolerance=±5% resistance=100 package="0805 [SMD]"]

nets:
  N1: Heltec_New_WiFi_Kit_1.pin_27, R1.Pin_0
  N2: Heltec_New_WiFi_Kit_1.pin_16, Heltec_New_WiFi_Kit_1.pin_20, D1.C
  N3: Heltec_New_WiFi_Kit_1.pin_18, Heltec_New_WiFi_Kit_1.pin_19, NEOPIXEL1.GND, JACK1.NEG, C1.-
  N4: Heltec_New_WiFi_Kit_1.pin_21, Heltec_New_WiFi_Kit_1.pin_15
  N5: NEOPIXEL1.Din, R1.Pin_1
  N6: NEOPIXEL1.+5V, JACK1.POS, C1.+, D1.A

notes:
  SEE NOTE!!!
  Pick one rail for *protected* 5V [red recommended], other rail for D5/DIN
  Keep LED Data and Power connections at opposite end of board
  1000uF
  Diode prevents USB from powering LEDs
  "Band towards board"
  There is no 3V3
  Pick one rail for *unprotected* 5V, one for ground
  *100* ohm resistor from D5 pin
  Level shifter not used

custom parts:
  Neopixel Strip -- Black (30/m): These NeoPixel strips have 30 digitally-addressable pixel LEDs per meter and are very affordable and are only 12.5 mm wide, 10 mm if you remove the strip from the casing.
