# Fritzing sketch arduino-Lesson7-WiringDiagram1-V2 (saved by Fritzing 0.9.6b)
breadboards: 1

parts:
  Heltec_New_WiFi_Kit_1 = Heltec New WiFi Kit 32 [part_number=ZC-47]
  R1 = Resistor [tolerance=±5% resistance=330 package="2512 [SMD]"]
  LED1 = smd LED [color="Red (633nm)" package="0603 [SMD]"]
  LED2 = smd LED [color="Green (555nm)" package="0603 [SMD]"]
  LED3 = smd LED [color="Blue (430nm)" package="0603 [SMD]"]

nets:
  N1: Heltec_New_WiFi_Kit_1.pin_16, Heltec_New_WiFi_Kit_1.pin_20
  N2: Heltec_New_WiFi_Kit_1.pin_18, Heltec_New_WiFi_Kit_1.pin_19, R1.Pin_1
  N3: Heltec_New_WiFi_Kit_1.pin_21, Heltec_New_WiFi_Kit_1.pin_15
  N4: Heltec_New_WiFi_Kit_1.pin_13, LED1.cathode
  N5: Heltec_New_WiFi_Kit_1.pin_14, LED2.cathode
  N6: Heltec_New_WiFi_Kit_1.pin_22, LED3.cathode
  N7: R1.Pin_0, LED1.anode, LED2.anode, LED3.anode
