# Fritzing sketch arduino-Lesson9-WiringDiagram-V2 (saved by Fritzing 0.9.6b)
breadboards: 1

parts:
  Heltec_New_WiFi_Kit_1 = Heltec New WiFi Kit 32 [part_number=ZC-47]
  J1 = JST-B3P-VH [part_number=JST-B3P-VH package=THT]
  NEOPIXEL1 = Neopixel Strip -- Black (30/m) [part_number=1376]
  JACK1 = 2.1mm Barrel Jack with Terminal Block
  C1 = Electrolytic Capacitor [capacitance=1000µF voltage=35V package="300 mil [THT, electrolytic]"]
  R1 = Resistor [tolerance=±5% resistance=470 package="2512 [SMD]"]
  D1 = Diode [package=diode-hv]

nets:
  N1: Heltec_New_WiFi_Kit_1.pin_27, R1.Pin_1
  N2: Heltec_New_WiFi_Kit_1.pin_16, Heltec_New_WiFi_Kit_1.pin_20, D1.C
  N3: Heltec_New_WiFi_Kit_1.pin_18, Heltec_New_WiFi_Kit_1.pin_19, J1.pin1, NEOPIXEL1.GND, JACK1.NEG, C1.-, D1.A
  N4: Heltec_New_WiFi_Kit_1.pin_21, Heltec_New_WiFi_Kit_1.pin_15
  N5: J1.pin2, NEOPIXEL1.Din, R1.Pin_0
  N6: J1.pin3, NEOPIXEL1.+5V, JACK1.POS, C1.+

notes:
  SEE NOTE!!!
  470 Ohm in-line with pin 5
  Pick one rail for the data line to the LED strip
  Keep LED and Power connections at opposite end of board
  1000uF
  Use the other rail for diode protected power to board
  Diode prevents USB from powering pixels
  "Band towards board"

custom parts:
  Neopixel Strip -- Black (30/m): These NeoPixel strips have 30 digitally-addressable pixel LEDs per meter and are very affordable and are only 12.5 mm wide, 10 mm if you remove the strip from the casing.
